// Logisim project cpu.circ as structural Verilog: 1 circuit, main circuit cpu
module cpu (
  input  clk,
  input  [31:0] INSTRUCTION,
  input  [31:0] READ_DATA,
  output [31:0] WRITE_ADDRESS,
  output [31:0] PROGRAM_COUNTER,
  output [31:0] ra,
  output [31:0] sp,
  output [31:0] t0,
  output [31:0] t1,
  output [31:0] t2,
  output [31:0] s0,
  output [31:0] s1,
  output [31:0] a0,
  output [31:0] tohost,
  output [3:0] WRITE_ENABLE,
  output [31:0] WRITE_DATA
);

  wire and_7_out, and_8_out, and_9_out, and_10_out, and_11_out, and_12_out, and_13_out, ASel, BrEq, BrLt,
       BrUn, BSel, \byte , comparator_2_eq, comparator_3_eq, comparator_4_eq, comparator_5_eq,
       comparator_6_eq, comparator_7_eq, comparator_8_eq, comparator_9_eq, comparator_10_eq,
       comparator_11_eq, comparator_12_eq, comparator_13_eq, comparator_14_eq, comparator_15_eq,
       comparator_16_eq, comparator_17_eq, comparator_18_eq, comparator_19_eq, CSRSel, CSRWen, half, MemRW,
       or_1_out, or_2_out, PCSel, RegWEn, sb, sh, store, sw, word;
  wire [1:0] ALU_out, WBSel;
  wire [2:0] ImmSel;
  wire [3:0] ALUSel, mask;
  wire [31:0] csr_din, imm, input_a, input_b, PC4, pc_in, read_reg1, Write_Data_t;

  Adder #(.width(32)) adder_1 (.a(PROGRAM_COUNTER), .b(32'h4), .out(PC4));  // open: cin, cout
  Register #(.width(32)) PC (.D(pc_in), .clk(clk), .Q(PROGRAM_COUNTER));  // open: en, clr
  Multiplexer #(.enable("false"), .width(32)) multiplexer_1 (
    .in0(PC4), .in1({WRITE_ADDRESS[31:2], ALU_out}), .out(pc_in), .sel(PCSel));
  control_logic control_logic_1 (
    .CSRWen(CSRWen), .PCSel(PCSel), .RegWEn(RegWEn), .ImmSel(ImmSel), .BrUn(BrUn), .ASel(ASel), .BSel(BSel),
    .ALUSel(ALUSel), .MemRW(MemRW), .WBSel(WBSel), .CSRSel(CSRSel), .inst(INSTRUCTION), .BrEq(BrEq),
    .BrLt(BrLt));
  imm_gen imm_gen_1 (.inst(INSTRUCTION), .ImmSel(ImmSel), .imm(imm));
  regfile regfile_1 (
    .rs1(INSTRUCTION[19:15]), .rs2(INSTRUCTION[24:20]), .rd(INSTRUCTION[11:7]), .Write_Data(Write_Data_t),
    .RegWEn(RegWEn), .clk(clk), .ra(ra), .sp(sp), .t0(t0), .t1(t1), .t2(t2), .s0(s0), .s1(s1), .a0(a0),
    .Read_Data_1(read_reg1), .Read_Data_2(WRITE_DATA));
  branch_comp branch_comp_1 (.rs1(read_reg1), .rs2(WRITE_DATA), .BrUn(BrUn), .BrEq(BrEq), .BrLt(BrLt));
  Multiplexer #(.enable("false"), .width(32)) multiplexer_2 (.in0(WRITE_DATA), .in1(imm), .out(input_b), .sel(BSel));
  Multiplexer #(.enable("false"), .width(32)) multiplexer_3 (
    .in0(PROGRAM_COUNTER), .in1(read_reg1), .out(input_a), .sel(ASel));
  Multiplexer #(.enable("false"), .select(3), .width(32)) multiplexer_4 (
    .in1(read_reg1), .in5(imm), .out(csr_din), .sel(INSTRUCTION[14:12]));  // open: in0, in2, in3, in4, in6, in7
  // csr csr_1: pin names not known; wires that end beside it: INSTRUCTION[31:20], csr_din, CSRWen, clk, tohost
  alu alu_1 (.Result({WRITE_ADDRESS[31:2], ALU_out}), .A(input_a), .B(input_b), .ALUSel(ALUSel));
  Comparator #(.width(7)) comparator_1 (.a(INSTRUCTION[6:0]), .b(7'b0100011), .eq(store));  // open: gt, lt
  Comparator #(.width(3)) comparator_2 (.a(INSTRUCTION[14:12]), .b(3'b010), .eq(comparator_2_eq));  // open: gt, lt
  Comparator #(.width(3)) comparator_3 (.a(INSTRUCTION[14:12]), .b(3'b001), .eq(comparator_3_eq));  // open: gt, lt
  Comparator #(.width(3)) comparator_4 (.a(INSTRUCTION[14:12]), .b(3'b000), .eq(comparator_4_eq));  // open: gt, lt
  and and_1 (sw, store, comparator_2_eq);
  and and_2 (sh, store, comparator_3_eq);
  and and_3 (sb, store, comparator_4_eq);
  Multiplexer #(.enable("false"), .width(4)) multiplexer_5 (.in0(4'b0000), .in1(mask), .out(WRITE_ENABLE), .sel(MemRW));
  Comparator #(.mode("unsigned"), .width(2)) comparator_5 (
    .a(ALU_out), .b(2'b10), .eq(comparator_5_eq));  // open: gt, lt
  Comparator #(.mode("unsigned"), .width(2)) comparator_6 (
    .a(ALU_out), .b(2'b01), .eq(comparator_6_eq));  // open: gt, lt
  Comparator #(.mode("unsigned"), .width(2)) comparator_7 (
    .a(ALU_out), .b(2'b00), .eq(comparator_7_eq));  // open: gt, lt
  Comparator #(.mode("unsigned"), .width(2)) comparator_8 (
    .a(ALU_out), .b(2'b10), .eq(comparator_8_eq));  // open: gt, lt
  Comparator #(.mode("unsigned"), .width(2)) comparator_9 (
    .a(ALU_out), .b(2'b01), .eq(comparator_9_eq));  // open: gt, lt
  Comparator #(.mode("unsigned"), .width(2)) comparator_10 (
    .a(ALU_out), .b(2'b00), .eq(comparator_10_eq));  // open: gt, lt
  Comparator #(.mode("unsigned"), .width(2)) comparator_11 (
    .a(ALU_out), .b(2'b11), .eq(comparator_11_eq));  // open: gt, lt
  Comparator #(.mode("unsigned"), .width(2)) comparator_12 (
    .a(ALU_out), .b(2'b00), .eq(comparator_12_eq));  // open: gt, lt
  and and_4 (word, comparator_7_eq, sw);
  or or_1 (or_1_out, comparator_8_eq, comparator_9_eq, comparator_10_eq);
  or or_2 (or_2_out, comparator_5_eq, comparator_6_eq, comparator_11_eq, comparator_12_eq);
  Multiplexer #(.enable("false"), .select(2), .width(32)) multiplexer_6 (
    .in0(PC4), .in1({WRITE_ADDRESS[31:2], ALU_out}), .in2(READ_DATA), .out(Write_Data_t), .sel(WBSel));  // open: in3
  and and_5 (half, or_1_out, sh);
  and and_6 (\byte , or_2_out, sb);
  and and_7 (and_7_out, half, comparator_13_eq);
  Multiplexer #(.enable("false"), .width(4)) multiplexer_7 (.in1(4'b1111), .out(mask), .sel(word));  // open: in0
  Multiplexer #(.enable("false"), .width(4)) multiplexer_8 (.in1(4'b1100), .out(mask), .sel(and_7_out));  // open: in0
  Comparator #(.mode("unsigned"), .width(2)) comparator_13 (
    .a(ALU_out), .b(2'b10), .eq(comparator_13_eq));  // open: gt, lt
  Multiplexer #(.enable("false"), .width(4)) multiplexer_9 (.in1(4'b0011), .out(mask), .sel(and_8_out));  // open: in0
  and and_8 (and_8_out, half, comparator_14_eq);
  Multiplexer #(.enable("false"), .width(4)) multiplexer_10 (.in1(4'b0110), .out(mask), .sel(and_9_out));  // open: in0
  and and_9 (and_9_out, half, comparator_15_eq);
  Multiplexer #(.enable("false"), .width(4)) multiplexer_11 (.in1(4'b0001), .out(mask), .sel(and_10_out));  // open: in0
  and and_10 (and_10_out, \byte , comparator_16_eq);
  Multiplexer #(.enable("false"), .width(4)) multiplexer_12 (.in1(4'b0100), .out(mask), .sel(and_11_out));  // open: in0
  and and_11 (and_11_out, \byte , comparator_17_eq);
  Comparator #(.mode("unsigned"), .width(2)) comparator_14 (
    .a(ALU_out), .b(2'b00), .eq(comparator_14_eq));  // open: gt, lt
  Comparator #(.mode("unsigned"), .width(2)) comparator_15 (
    .a(ALU_out), .b(2'b01), .eq(comparator_15_eq));  // open: gt, lt
  Comparator #(.mode("unsigned"), .width(2)) comparator_16 (
    .a(ALU_out), .b(2'b00), .eq(comparator_16_eq));  // open: gt, lt
  Comparator #(.mode("unsigned"), .width(2)) comparator_17 (
    .a(ALU_out), .b(2'b10), .eq(comparator_17_eq));  // open: gt, lt
  and and_12 (and_12_out, \byte , comparator_18_eq);
  and and_13 (and_13_out, \byte , comparator_19_eq);
  Multiplexer #(.enable("false"), .width(4)) multiplexer_13 (.in1(4'b0010), .out(mask), .sel(and_12_out));  // open: in0
  Multiplexer #(.enable("false"), .width(4)) multiplexer_14 (.in1(4'b1000), .out(mask), .sel(and_13_out));  // open: in0
  Comparator #(.mode("unsigned"), .width(2)) comparator_18 (
    .a(ALU_out), .b(2'b01), .eq(comparator_18_eq));  // open: gt, lt
  Comparator #(.mode("unsigned"), .width(2)) comparator_19 (
    .a(ALU_out), .b(2'b11), .eq(comparator_19_eq));  // open: gt, lt

  assign WRITE_ADDRESS[1:0] = 2'b00;

  // Other names for the same wires on the sheet: csr_addr[11:0] = INSTRUCTION[31:20]; inst[31:0] = INSTRUCTION;
  //   rs2[4:0] = INSTRUCTION[24:20]; funct3[2:0] = INSTRUCTION[14:12]; rd[4:0] = INSTRUCTION[11:7];
  //   rs1[4:0] = INSTRUCTION[19:15]; opcode[6:0] = INSTRUCTION[6:0]; read_reg2[31:0] = WRITE_DATA;
  //   last2bits[1:0] = ALU_out; wr_addr[31:0] = {WRITE_ADDRESS[31:2], ALU_out}; ALU_out[31:2] = WRITE_ADDRESS[31:2]

  // Notes on the sheet:
  //   Output to IMEM
  //   IMEM (do **NOT** move this)
  //   Inputs from IMEM
  //   It is OK to move the PC, RegFile, ALU, MEM, Branch Comp, Imm Gen, and Control Logic to wherever is most convenient for you when constructing your CPU, and to delete this text
  //   Inputs/Outputs for testing. Do **NOT** move these.
  //   Outputs To DMEM
  //   DMEM (do **NOT** move this)
  //   Inputs From DMEM
endmodule
