// Logisim project imm-gen.circ as structural Verilog: 1 circuit, main circuit imm_gen
module imm_gen (
  input  [31:0] inst,
  input  [2:0] ImmSel,
  output [31:0] imm
);

  wire [31:0] csrwi_type, i_type;
  wire [31:5] s_type;
  wire [31:12] b_type;
  wire [31:20] j_type;

  assign b_type = {{19{inst[31]}}, inst[31]};  // Bit_Extender bit_extender_1
  assign j_type = {{11{inst[31]}}, inst[31]};  // Bit_Extender bit_extender_2
  assign csrwi_type = {{27{1'b0}}, inst[19:15]};  // Bit_Extender bit_extender_3
  assign i_type = {{20{inst[31]}}, inst[31:20]};  // Bit_Extender bit_extender_4
  assign s_type = {{20{inst[31]}}, inst[31:25]};  // Bit_Extender bit_extender_5
  Multiplexer #(.enable("false"), .select(3), .width(32)) multiplexer_1 (
    .in0(i_type), .in1({s_type, inst[11:7]}), .in2({b_type, inst[7], inst[30:25], inst[11:8], 1'b0}),
    .in3({inst[31:12], {12{1'b0}}}), .in4({j_type, inst[19:12], inst[20], inst[30:21], 1'b0}),
    .in5(csrwi_type), .out(imm), .sel(ImmSel));  // open: in6, in7

  // Other names for the same wires on the sheet: instr_21[9:0] = inst[30:21];
  //   j_type[19:1] = {inst[19:12], inst[20], inst[30:21]}; u_type[31:12] = inst[31:12];
  //   b_type[11:1] = {inst[7], inst[30:25], inst[11:8]}; instr_20 = inst[20]; instr_12[7:0] = inst[19:12];
  //   instr_7 = inst[7]; s_type[4:0] = inst[11:7]

  // Notes on the sheet:
  //   INPUTS to your circuit
  //   DON'T CHANGE THE LOCATIONS OF THE INPUTS AND OUTPUTS!
  //   OUTPUT from your circuit
endmodule
