// Logisim project regfile.circ as structural Verilog: 1 circuit, main circuit regfile
module regfile (
  input  [4:0] rs1,
  input  [4:0] rs2,
  input  [4:0] rd,
  input  [31:0] Write_Data,
  input  RegWEn,
  input  clk,
  output [31:0] ra,
  output [31:0] sp,
  output [31:0] t0,
  output [31:0] t1,
  output [31:0] t2,
  output [31:0] s0,
  output [31:0] s1,
  output [31:0] a0,
  output [31:0] Read_Data_1,
  output [31:0] Read_Data_2
);

  wire x1_WrEn, x2_WrEn, x3_WrEn, x4_WrEn, x5_WrEn, x6_WrEn, x7_WrEn, x8_WrEn, x9_WrEn, x10_WrEn, x11_WrEn,
       x12_WrEn, x13_WrEn, x14_WrEn, x15_WrEn, x16_WrEn, x17_WrEn, x18_WrEn, x19_WrEn, x20_WrEn, x21_WrEn,
       x22_WrEn, x23_WrEn, x24_WrEn, x25_WrEn, x26_WrEn, x27_WrEn, x28_WrEn, x29_WrEn, x30_WrEn, x31_WrEn;
  wire [31:0] x0, x3, x4, x11, x12, x13, x14, x15, x16, x17, x18, x19, x20, x21, x22, x23, x24, x25, x26,
       x27, x28, x29, x30, x31;

  Demultiplexer #(.enable("false"), .select(5)) demultiplexer_1 (
    .out1(x1_WrEn), .out2(x2_WrEn), .out3(x3_WrEn), .out4(x4_WrEn), .out5(x5_WrEn), .out6(x6_WrEn),
    .out7(x7_WrEn), .out8(x8_WrEn), .out9(x9_WrEn), .out10(x10_WrEn), .out11(x11_WrEn), .out12(x12_WrEn),
    .out13(x13_WrEn), .out14(x14_WrEn), .out15(x15_WrEn), .out16(x16_WrEn), .out17(x17_WrEn),
    .out18(x18_WrEn), .out19(x19_WrEn), .out20(x20_WrEn), .out21(x21_WrEn), .out22(x22_WrEn),
    .out23(x23_WrEn), .out24(x24_WrEn), .out25(x25_WrEn), .out26(x26_WrEn), .out27(x27_WrEn),
    .out28(x28_WrEn), .out29(x29_WrEn), .out30(x30_WrEn), .out31(x31_WrEn), .in(RegWEn), .sel(rd));  // open: out0
  Register #(.width(32)) u_x0 (.D(Write_Data), .clk(clk), .Q(x0), .clr(1'b1));  // open: en
  Register #(.width(32)) u_x4 (.D(Write_Data), .en(x4_WrEn), .clk(clk), .Q(x4));  // open: clr
  Register #(.width(32)) x8_s0 (.D(Write_Data), .en(x8_WrEn), .clk(clk), .Q(s0));  // open: clr
  Register #(.width(32)) u_x12 (.D(Write_Data), .en(x12_WrEn), .clk(clk), .Q(x12));  // open: clr
  Register #(.width(32)) u_x16 (.D(Write_Data), .en(x16_WrEn), .clk(clk), .Q(x16));  // open: clr
  Register #(.width(32)) u_x20 (.D(Write_Data), .en(x20_WrEn), .clk(clk), .Q(x20));  // open: clr
  Register #(.width(32)) u_x24 (.D(Write_Data), .en(x24_WrEn), .clk(clk), .Q(x24));  // open: clr
  Register #(.width(32)) u_x28 (.D(Write_Data), .en(x28_WrEn), .clk(clk), .Q(x28));  // open: clr
  Register #(.width(32)) x1_ra (.D(Write_Data), .en(x1_WrEn), .clk(clk), .Q(ra));  // open: clr
  Register #(.width(32)) x5_t0 (.D(Write_Data), .en(x5_WrEn), .clk(clk), .Q(t0));  // open: clr
  Register #(.width(32)) x9_s1 (.D(Write_Data), .en(x9_WrEn), .clk(clk), .Q(s1));  // open: clr
  Register #(.width(32)) u_x13 (.D(Write_Data), .en(x13_WrEn), .clk(clk), .Q(x13));  // open: clr
  Register #(.width(32)) u_x17 (.D(Write_Data), .en(x17_WrEn), .clk(clk), .Q(x17));  // open: clr
  Register #(.width(32)) u_x21 (.D(Write_Data), .en(x21_WrEn), .clk(clk), .Q(x21));  // open: clr
  Register #(.width(32)) u_x25 (.D(Write_Data), .en(x25_WrEn), .clk(clk), .Q(x25));  // open: clr
  Register #(.width(32)) u_x29 (.D(Write_Data), .en(x29_WrEn), .clk(clk), .Q(x29));  // open: clr
  Register #(.width(32)) x2_sp (.D(Write_Data), .en(x2_WrEn), .clk(clk), .Q(sp));  // open: clr
  Register #(.width(32)) x6_t1 (.D(Write_Data), .en(x6_WrEn), .clk(clk), .Q(t1));  // open: clr
  Register #(.width(32)) x10_a0 (.D(Write_Data), .en(x10_WrEn), .clk(clk), .Q(a0));  // open: clr
  Register #(.width(32)) u_x14 (.D(Write_Data), .en(x14_WrEn), .clk(clk), .Q(x14));  // open: clr
  Register #(.width(32)) u_x18 (.D(Write_Data), .en(x18_WrEn), .clk(clk), .Q(x18));  // open: clr
  Register #(.width(32)) u_x22 (.D(Write_Data), .en(x22_WrEn), .clk(clk), .Q(x22));  // open: clr
  Register #(.width(32)) u_x26 (.D(Write_Data), .en(x26_WrEn), .clk(clk), .Q(x26));  // open: clr
  Register #(.width(32)) u_x30 (.D(Write_Data), .en(x30_WrEn), .clk(clk), .Q(x30));  // open: clr
  Multiplexer #(.enable("false"), .select(5), .width(32)) multiplexer_1 (
    .in0(x0), .in1(ra), .in2(sp), .in3(x3), .in4(x4), .in5(t0), .in6(t1), .in7(t2), .in8(s0), .in9(s1),
    .in10(a0), .in11(x11), .in12(x12), .in13(x13), .in14(x14), .in15(x15), .in16(x16), .in17(x17),
    .in18(x18), .in19(x19), .in20(x20), .in21(x21), .in22(x22), .in23(x23), .in24(x24), .in25(x25),
    .in26(x26), .in27(x27), .in28(x28), .in29(x29), .in30(x30), .in31(x31), .out(Read_Data_1), .sel(rs1));
  Register #(.width(32)) u_x3 (.D(Write_Data), .en(x3_WrEn), .clk(clk), .Q(x3));  // open: clr
  Register #(.width(32)) x7_t2 (.D(Write_Data), .en(x7_WrEn), .clk(clk), .Q(t2));  // open: clr
  Register #(.width(32)) u_x11 (.D(Write_Data), .en(x11_WrEn), .clk(clk), .Q(x11));  // open: clr
  Register #(.width(32)) u_x15 (.D(Write_Data), .en(x15_WrEn), .clk(clk), .Q(x15));  // open: clr
  Register #(.width(32)) u_x19 (.D(Write_Data), .en(x19_WrEn), .clk(clk), .Q(x19));  // open: clr
  Register #(.width(32)) u_x23 (.D(Write_Data), .en(x23_WrEn), .clk(clk), .Q(x23));  // open: clr
  Register #(.width(32)) u_x27 (.D(Write_Data), .en(x27_WrEn), .clk(clk), .Q(x27));  // open: clr
  Register #(.width(32)) u_x31 (.D(Write_Data), .en(x31_WrEn), .clk(clk), .Q(x31));  // open: clr
  Multiplexer #(.enable("false"), .select(5), .width(32)) multiplexer_2 (
    .in0(x0), .in1(ra), .in2(sp), .in3(x3), .in4(x4), .in5(t0), .in6(t1), .in7(t2), .in8(s0), .in9(s1),
    .in10(a0), .in11(x11), .in12(x12), .in13(x13), .in14(x14), .in15(x15), .in16(x16), .in17(x17),
    .in18(x18), .in19(x19), .in20(x20), .in21(x21), .in22(x22), .in23(x23), .in24(x24), .in25(x25),
    .in26(x26), .in27(x27), .in28(x28), .in29(x29), .in30(x30), .in31(x31), .out(Read_Data_2), .sel(rs2));

  // Other names for the same wires on the sheet: read_data1[31:0] = Read_Data_1; read_data2[31:0] = Read_Data_2;
  //   read_reg1[4:0] = rs1; read_reg2[4:0] = rs2; write_en = RegWEn; write_reg[4:0] = rd

  // Notes on the sheet:
  //   INPUTS to your circuit
  //   DON'T CHANGE THE LOCATIONS OF THE INPUTS AND OUTPUTS!
  //   These are DEBUG/TEST outputs from your circuit.
  //   OUTPUTS from your circuit
endmodule
