// Logisim project cpu-jump_edge.circ as structural Verilog: 1 circuit, main circuit run_main
module run_main (
  output [31:0] ra,
  output [31:0] sp,
  output [31:0] t0,
  output [31:0] t1,
  output [31:0] t2,
  output [31:0] s0,
  output [31:0] s1,
  output [31:0] a0,
  output [31:0] Requested_Address,
  output [31:0] Requested_Instruction,
  output [15:0] Time_Step,
  output halt
);

  wire clk;

  Clock clock_1 (.out(clk));
  // Probe on Requested_Address
  // cpu_harness cpu_harness_1: pin names not known; wires that end beside it: Requested_Instruction, clk, Requested_Address, ra, sp, t0, t1, t2, s0, s1, a0
  ROM #(.addrWidth(14), .dataWidth(32)) rom_1 (.addr(Requested_Address[15:2]), .data(Requested_Instruction));
  // Probe on Requested_Instruction
  Counter #(.max('hffff), .width(16)) counter_1 (.clk(clk), .Q(Time_Step));  // open: clr, load, up, count, D, carry
  Comparator #(.width(16)) comparator_1 (.a(Time_Step), .b(16'h7), .eq(halt));  // open: gt, lt

  // Other names for the same wires on the sheet: INSTRUCTION[31:0] = Requested_Instruction;
  //   PROGRAM_COUNTER[31:0] = Requested_Address

  // Notes on the sheet:
  //   contents of rom_1 (hex, n*v repeats v):
  //   7050F0EF 500093 FF600113 2080B3 2109133 6400193 FFD00213 404181B3 322233 FF200293 1400313 26292B3
  //   22636313 F8300393 D6500413 83F3B3 40745433 4A00493 FDD00513 951533 24D493 7FF00593 80000613 C585B3
  //   83062613 EA00613 100693 D66633 26F693 DD400713 A00793 2F71733 FF67C793 1300813 5B00893 10898B3
  //   1180833 FD800913 16F00993 41390933 7D09A993 7D100A13 7D000A93 15A7A33 FADA93 30900B13 37800B93
  //   37B1B33 16BCBB3 C1800C13 1F900C93 405C5C13 3C9C93 FE200D13 6400D93 3BD3D33 41AD8DB3 500E13 700E93
  //   1DE0E33 AEAE93 A00F13 E0C00F93 3FF3F33 1EF8FB3 500093 FF600113 2080B3 2109133 6400193 FFD00213
  //   404181B3 322233 FF200293 1400313 26292B3 22636313 F8300393 D6500413 83F3B3 40745433 4A00493 FDD00513
  //   951533 24D493 7FF00593 80000613 C585B3 83062613 EA00613 100693 D66633 26F693 DD400713 A00793 2F71733
  //   FF67C793 1300813 5B00893 10898B3 1180833 FD800913 16F00993 41390933 7D09A993 7D100A13 7D000A93
  //   15A7A33 FADA93 30900B13 37800B93 37B1B33 16BCBB3 C1800C13 1F900C93 405C5C13 3C9C93 FE200D13 6400D93
  //   3BD3D33 41AD8DB3 500E13 700E93 1DE0E33 AEAE93 A00F13 E0C00F93 3FF3F33 1EF8FB3 500093 FF600113 2080B3
  //   2109133 6400193 FFD00213 404181B3 322233 FF200293 1400313 26292B3 22636313 F8300393 D6500413 83F3B3
  //   40745433 4A00493 FDD00513 951533 24D493 7FF00593 80000613 C585B3 83062613 EA00613 100693 D66633
  //   26F693 DD400713 A00793 2F71733 FF67C793 1300813 5B00893 10898B3 1180833 FD800913 16F00993 41390933
  //   7D09A993 7D100A13 7D000A93 15A7A33 FADA93 30900B13 37800B93 37B1B33 16BCBB3 C1800C13 1F900C93
  //   405C5C13 3C9C93 FE200D13 6400D93 3BD3D33 41AD8DB3 500E13 700E93 1DE0E33 AEAE93 A00F13 E0C00F93
  //   3FF3F33 1EF8FB3 500093 FF600113 2080B3 2109133 6400193 FFD00213 404181B3 322233 FF200293 1400313
  //   26292B3 22636313 F8300393 D6500413 83F3B3 40745433 4A00493 FDD00513 951533 24D493 7FF00593 80000613
  //   C585B3 83062613 EA00613 100693 D66633 26F693 DD400713 A00793 2F71733 FF67C793 1300813 5B00893
  //   10898B3 1180833 FD800913 16F00993 41390933 7D09A993 7D100A13 7D000A93 15A7A33 FADA93 30900B13
  //   37800B93 37B1B33 16BCBB3 C1800C13 1F900C93 405C5C13 3C9C93 FE200D13 6400D93 3BD3D33 41AD8DB3 500E13
  //   700E93 1DE0E33 AEAE93 A00F13 E0C00F93 3FF3F33 1EF8FB3 500093 FF600113 2080B3 2109133 6400193
  //   FFD00213 404181B3 322233 FF200293 1400313 26292B3 22636313 F8300393 D6500413 83F3B3 40745433 4A00493
  //   FDD00513 951533 24D493 7FF00593 80000613 C585B3 83062613 EA00613 100693 D66633 26F693 DD400713
  //   A00793 2F71733 FF67C793 1300813 5B00893 10898B3 1180833 FD800913 16F00993 41390933 7D09A993 7D100A13
  //   7D000A93 15A7A33 FADA93 30900B13 37800B93 37B1B33 16BCBB3 C1800C13 1F900C93 405C5C13 3C9C93 FE200D13
  //   6400D93 3BD3D33 41AD8DB3 500E13 700E93 1DE0E33 AEAE93 A00F13 E0C00F93 3FF3F33 1EF8FB3 500093
  //   FF600113 2080B3 2109133 6400193 FFD00213 404181B3 322233 FF200293 1400313 26292B3 22636313 F8300393
  //   D6500413 83F3B3 40745433 4A00493 FDD00513 951533 24D493 7FF00593 80000613 C585B3 83062613 EA00613
  //   100693 D66633 26F693 DD400713 A00793 2F71733 FF67C793 1300813 5B00893 10898B3 1180833 FD800913
  //   16F00993 41390933 7D09A993 7D100A13 7D000A93 15A7A33 FADA93 30900B13 37800B93 37B1B33 16BCBB3
  //   C1800C13 1F900C93 405C5C13 3C9C93 FE200D13 6400D93 3BD3D33 41AD8DB3 500E13 700E93 1DE0E33 AEAE93
  //   A00F13 E0C00F93 3FF3F33 1EF8FB3 500093 FF600113 2080B3 2109133 6400193 FFD00213 404181B3 322233
  //   FF200293 1400313 26292B3 22636313 F8300393 D6500413 83F3B3 40745433 4A00493 FDD00513 951533 24D493
  //   7FF00593 80000613 C585B3 83062613 EA00613 100693 D66633 26F693 DD400713 A00793 2F71733 FF67C793
  //   1300813 5B00893 10898B3 1180833 FD800913 16F00993 41390933 7D09A993 7D100A13 7D000A93 15A7A33 FADA93
  //   30900B13 37800B93 37B1B33 16BCBB3 C1800C13 1F900C93 405C5C13 3C9C93 FE200D13 6400D93 3BD3D33
  //   41AD8DB3 500E13 700E93 1DE0E33 AEAE93 A00F13 E0C00F93 3FF3F33 1EF8FB3 500093 FF600113 2080B3 2109133
  //   6400193 FFD00213 404181B3 322233 FF200293 1400313 26292B3 22636313 F8300393 D6500413 83F3B3 40745433
  //   4A00493 FDD00513 951533 24D493 7FF00593 80000613 C585B3 83062613 EA00613 100693 D66633 26F693
  //   DD400713 A00793 2F71733 FF67C793 1300813 5B00893 10898B3 1180833 FD800913 16F00993 41390933 7D09A993
  //   7D1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
  //   Instruction Memory
  //   Halts Execution After Constant # of Clock Cycles
  //   Constant
endmodule
